// Logisim project Logism.circ as structural Verilog: 1 circuit, main circuit main
module main (
  input  x,
  input  y,
  output F
);

  and and_1 (F, x, y);

  // Notes on the sheet:
  //   Элемент И
endmodule
