// Logisim project polusummator_i_summator.circ as structural Verilog: 1 circuit, main circuit main
module main (
  input  A,
  input  B,
  input  \А ,
  input  \В ,
  input  \Р ,
  output out_6,
  output P,
  output S,
  output P_2
);

  wire and_1_out, and_2_out, and_3_out, and_4_out, and_6_out, and_7_out, not_1_out, not_2_out, not_3_out,
       or_1_out, or_2_out;

  not not_1 (not_1_out, B);
  not not_2 (not_2_out, A);
  and and_1 (and_1_out, \А , \В );
  or or_1 (or_1_out, \А , \В );
  and and_2 (and_2_out, or_1_out, \Р );
  and and_3 (and_3_out, A, not_1_out);
  and and_4 (and_4_out, not_2_out, B);
  and and_5 (P, A, B);
  and and_6 (and_6_out, and_1_out, \Р );
  or or_2 (or_2_out, \Р , or_1_out);
  or or_3 (P_2, and_1_out, and_2_out);
  not not_3 (not_3_out, P_2);
  or or_4 (out_6, and_3_out, and_4_out);
  and and_7 (and_7_out, or_2_out, not_3_out);
  or or_5 (S, and_6_out, and_7_out);
endmodule
