// Logisim project taaask1.circ as structural Verilog: 1 circuit, main circuit main
module main (
  input  r,
  input  s,
  input  s_2,
  input  c,
  input  r_2,
  input  c_2,
  input  d,
  output q,
  output q_prime,
  output q_2,
  output q_prime_2,
  output q_3,
  output q_prime_3
);

  wire and_1_out, and_2_out, and_3_out, and_4_out, not_1_out;

  nor nor_1 (q, r, q_prime);
  nor nor_2 (q_prime, q, s);
  and and_1 (and_1_out, s_2, c);
  and and_2 (and_2_out, c, r_2);
  not not_1 (not_1_out, d);
  nor nor_3 (q_2, and_1_out, q_prime_2);
  nor nor_4 (q_prime_2, q_2, and_2_out);
  and and_3 (and_3_out, not_1_out, c_2);
  and and_4 (and_4_out, c_2, d);
  nor nor_5 (q_3, and_3_out, q_prime_3);
  nor nor_6 (q_prime_3, q_3, and_4_out);

  // Notes on the sheet:
  //   синхронный rs-триггер
  //   ассинхронный rs-триггер
  //   d-триггер
endmodule
