// Logisim project task1_scheme2.circ as structural Verilog: 1 circuit, main circuit main
module main (
  input  x,
  input  y,
  input  z,
  output f
);

  wire and_1_out, and_2_out, not_1_out, not_2_out, not_3_out, or_1_out, or_2_out, or_3_out, or_4_out;

  not not_1 (not_1_out, x);
  not not_2 (not_2_out, y);
  not not_3 (not_3_out, z);
  or or_1 (or_1_out, not_3_out, z);
  and and_1 (and_1_out, not_1_out, and_2_out);
  and and_2 (and_2_out, y, or_1_out);
  or or_2 (or_2_out, not_2_out, and_1_out);
  or or_3 (or_3_out, not_1_out, or_2_out);
  or or_4 (or_4_out, or_3_out, not_3_out);
  or or_5 (f, x, or_4_out);

  // Notes on the sheet:
  //   СХЕМА 2
endmodule
