// Logisim project task3-1.circ as structural Verilog: 1 circuit, main circuit main
module main (
  input  D4,
  input  D3,
  input  D2,
  input  D1,
  input  D0,
  input  C,
  input  E,
  output out_8,
  output out_9,
  output out_10,
  output out_11,
  output out_12,
  output out_13,
  output out_14,
  output out_15,
  output out_16,
  output out_17
);

  D_Flip_Flop d_ff_1 (.Q(out_8), .Qn(out_9), .preset(D4), .en(E), .reset(C));  // open: clk, D
  D_Flip_Flop d_ff_2 (.Q(out_10), .Qn(out_11), .preset(D3), .en(E), .reset(C));  // open: clk, D
  D_Flip_Flop d_ff_3 (.Q(out_12), .Qn(out_13), .preset(D2), .en(E), .reset(C));  // open: clk, D
  D_Flip_Flop d_ff_4 (.Q(out_14), .Qn(out_15), .preset(D1), .en(E), .reset(C));  // open: clk, D
  D_Flip_Flop d_ff_5 (.Q(out_16), .Qn(out_17), .preset(D0), .en(E), .reset(C));  // open: clk, D
endmodule
