// Logisim project work.circ as structural Verilog: 1 circuit, main circuit main
module main (
  input  A2,
  input  A1,
  input  A0,
  input  E,
  output out_5,
  output out_6,
  output out_7,
  output out_8,
  output out_9,
  output out_10,
  output out_11,
  output out_12
);

  wire and_1_out, and_2_out, and_3_out, and_4_out, and_5_out, and_6_out, and_7_out, and_8_out, not_1_out,
       not_2_out, not_3_out;

  not not_1 (not_1_out, A2);
  not not_2 (not_2_out, A0);
  not not_3 (not_3_out, A1);
  and and_1 (and_1_out, A2, A1, A0);
  and and_2 (and_2_out, A2, A1, not_2_out);
  and and_3 (and_3_out, A2, not_3_out, A0);
  and and_4 (and_4_out, A2, not_3_out, not_2_out);
  and and_5 (and_5_out, not_1_out, A1, A0);
  and and_6 (and_6_out, A1, not_1_out, not_2_out);
  and and_7 (and_7_out, A0, not_1_out, not_3_out);
  and and_8 (and_8_out, not_2_out, not_3_out, not_1_out);
  and D7 (out_5, and_1_out, E);
  and D6 (out_6, and_2_out, E);
  and D5 (out_7, and_3_out, E);
  and D4 (out_8, and_4_out, E);
  and D3 (out_9, and_5_out, E);
  and D2 (out_10, and_6_out, E);
  and D1 (out_11, and_7_out, E);
  and D0 (out_12, and_8_out, E);
endmodule
