// Logisim project work2.circ as structural Verilog: 1 circuit, main circuit main
module main (
  input  in_1,
  input  A7,
  input  A6,
  input  A5,
  input  A4,
  input  A3,
  input  A2,
  input  A1,
  input  A0,
  input  \А0 ,
  input  A1_2,
  input  A2_2,
  output out_13
);

  wire and_1_out, and_2_out, and_3_out, and_4_out, and_5_out, and_6_out, and_7_out, and_8_out, not_1_out,
       not_2_out, not_3_out, or_1_out, or_2_out;

  not not_1 (not_1_out, A1_2);
  not not_2 (not_2_out, \А0 );
  not not_3 (not_3_out, A2_2);
  and and_1 (and_1_out, A7, not_2_out, not_1_out, A2_2, in_1);
  and and_2 (and_2_out, in_1, not_2_out, A2_2, not_3_out, A6);
  and and_3 (and_3_out, in_1, not_2_out, A2_2, A1_2, A5);
  and and_4 (and_4_out, in_1, not_2_out, A1_2, A2_2, A4);
  and and_5 (and_5_out, in_1, \А0 , not_1_out, A2_2, A3);
  and and_6 (and_6_out, in_1, \А0 , not_1_out, A2_2, A2);
  and and_7 (and_7_out, in_1, \А0 , not_1_out, A2_2, A1);
  and and_8 (and_8_out, in_1, \А0 , A1_2, A2_2, A0);
  or or_1 (or_1_out, and_1_out, and_2_out, and_3_out, and_4_out, and_5_out);
  or or_2 (or_2_out, and_6_out, and_7_out, and_8_out);
  or or_3 (out_13, or_1_out, or_2_out);
endmodule
