// Logisim project пр1.1.circ as structural Verilog: 1 circuit, main circuit main
module main (
  input  X,
  input  Y,
  input  Z,
  output out_4
);

  wire and_1_out, and_2_out, not_1_out, not_2_out, not_3_out, or_1_out, or_2_out, or_3_out, or_4_out;

  not not_1 (not_1_out, X);
  not not_2 (not_2_out, Z);
  not not_3 (not_3_out, Y);
  or or_1 (or_1_out, not_1_out, X);
  and and_1 (and_1_out, or_1_out, Y);
  and and_2 (and_2_out, and_1_out, Z);
  or or_2 (or_2_out, and_2_out, not_2_out);
  or or_3 (or_3_out, or_2_out, not_3_out);
  or or_4 (or_4_out, or_3_out, Z);
  or or_5 (out_4, X, or_4_out);
endmodule
