// Logisim project пр1.2.circ as structural Verilog: 1 circuit, main circuit main
module main (
  input  x,
  input  y,
  input  z,
  output out_4
);

  wire and_1_out, and_2_out, not_1_out, not_2_out, not_3_out, or_1_out, or_2_out, or_3_out, or_4_out;

  not not_1 (not_1_out, x);
  not not_2 (not_2_out, y);
  not not_3 (not_3_out, z);
  or or_1 (or_1_out, z, not_3_out);
  and and_1 (and_1_out, not_1_out, and_2_out);
  and and_2 (and_2_out, not_2_out, or_1_out);
  or or_2 (or_2_out, and_1_out, not_2_out);
  or or_3 (or_3_out, not_1_out, or_2_out);
  or or_4 (or_4_out, or_3_out, not_3_out);
  or or_5 (out_4, x, or_4_out);
endmodule
