// Logisim project пр2.circ as structural Verilog: 1 circuit, main circuit main
module main (
  input  R,
  input  S,
  input  R_2,
  input  C,
  input  S_2,
  input  in_6,
  input  D,
  output Q,
  output out_9,
  output Q_2,
  output out_11,
  output Q_3,
  output out_13
);

  wire and_1_out, and_2_out, and_3_out, and_4_out, not_1_out;

  and and_1 (and_1_out, R_2, C);
  and and_2 (and_2_out, C, S_2);
  not not_1 (not_1_out, D);
  nor nor_1 (Q, R, out_9);
  nor nor_2 (out_9, Q, S);
  and and_3 (and_3_out, not_1_out, in_6);
  and and_4 (and_4_out, in_6, D);
  nor nor_3 (Q_2, and_1_out, out_11);
  nor nor_4 (out_11, Q_2, and_2_out);
  nor nor_5 (Q_3, and_3_out, out_13);
  nor nor_6 (out_13, Q_3, and_4_out);

  // Notes on the sheet:
  //   Асинхронный RS-тригер
  //   Синхронный RS-тригер
  //   D-тригер
endmodule
